# Fritzing sketch pocketbeagle-cp2102-serial-connector (saved by Fritzing 0.9.2b)

parts:
  Part1 = USB converter CP2102
  Part2 = PocketBeagle
  J1 = male pin header, 6 pins [form="♂ (male)"]
  J2 = female pin header, 6 pins [form="♀ (female)"]
  J3 = female pin header, 6 pins [form="♀ (female)"]
  J5 = male pin header, 1 pin [form="♂ (male)"]
  J4 = male pin header, 2 pins [form="♂ (male)"]

nets:
  N1: Part1.+5V, J1.pin6
  N2: Part1.GND, J1.pin5
  N3: Part1.TXO, J1.pin4
  N4: Part1.RXI, J1.pin3
  N5: Part1.DTR, J1.pin2
  N6: Part1.3V3, J1.pin1
  GND: Part2.GND, J5.pin1
  N7: Part2.UART0.TX, J4.pin1
  N8: Part2.UART0.RX, J4.pin2
  N9: J2.pin3, J3.pin5
  N10: J2.pin4, J3.pin6
  N11: J2.pin5, J3.pin1
