# Fritzing sketch pocketbeagle-usb-type-a (saved by Fritzing 0.9.2b)

parts:
  Part1 = USB type A female breakout module
  Part2 = PocketBeagle

nets:
  N1: Part1.VCC, Part2.USB1.VBUS, Part2.USB1.VIN
  N2: Part1.D-, Part2.USB1.DN
  N3: Part1.D+, Part2.USB1.DP
  GND: Part1.GND, Part2.USB1.ID, Part2.GND
